// Digital circuit ALU.dig as structural Verilog
module ALU (
  input  [7:0] N,
  input  [2:0] \Escolher_a_operação ,
  input  \Divisão_ou_Multiplicação ,
  input  Clock_MQ,
  input  Clock_AC,
  output [7:0] Resultado_AC,
  output [7:0] Resultado_MQ
);

  wire [7:0] Divisor_q0, Divisor_r7, multiplexer_1_out, multiplexer_2_out, Multiplicador_ac7,
       Multiplicador_mq7, Nand_out0, Shift_Left_out7, Shift_Right_out7, Somador_c8, \Subtartor__7º , Xor_out0;

  ShiftRight8BITs Shift_Right (
    .A0(Resultado_AC[0]), .A1(Resultado_AC[1]), .A2(Resultado_AC[2]), .A3(Resultado_AC[3]),
    .A4(Resultado_AC[4]), .A5(Resultado_AC[5]), .A6(Resultado_AC[6]), .A7(Resultado_AC[7]),
    .Out0(Shift_Right_out7[0]), .Out1(Shift_Right_out7[1]), .Out2(Shift_Right_out7[2]),
    .Out3(Shift_Right_out7[3]), .Out4(Shift_Right_out7[4]), .Out5(Shift_Right_out7[5]),
    .Out6(Shift_Right_out7[6]), .Out7(Shift_Right_out7[7]));
  ShiftLeft8BITs Shift_Left (
    .A0(Resultado_AC[0]), .A1(Resultado_AC[1]), .A2(Resultado_AC[2]), .A3(Resultado_AC[3]),
    .A4(Resultado_AC[4]), .A5(Resultado_AC[5]), .A6(Resultado_AC[6]), .A7(Resultado_AC[7]),
    .Out0(Shift_Left_out7[0]), .Out1(Shift_Left_out7[1]), .Out2(Shift_Left_out7[2]),
    .Out3(Shift_Left_out7[3]), .Out4(Shift_Left_out7[4]), .Out5(Shift_Left_out7[5]),
    .Out6(Shift_Left_out7[6]), .Out7(Shift_Left_out7[7]));
  Divisor8BITs Divisor (
    .Sor0(N[0]), .Sor1(N[1]), .Sor2(N[2]), .Sor3(N[3]), .Sor4(N[4]), .Sor5(N[5]), .Sor6(N[6]), .Sor7(N[7]),
    .Endo0(Resultado_AC[0]), .Endo1(Resultado_AC[1]), .Endo2(Resultado_AC[2]), .Endo3(Resultado_AC[3]),
    .Endo4(Resultado_AC[4]), .Endo5(Resultado_AC[5]), .Endo6(Resultado_AC[6]), .Endo7(Resultado_AC[7]),
    .Q7(Divisor_q0[7]), .Q6(Divisor_q0[6]), .Q5(Divisor_q0[5]), .Q4(Divisor_q0[4]), .Q3(Divisor_q0[3]),
    .Q2(Divisor_q0[2]), .Q1(Divisor_q0[1]), .Q0(Divisor_q0[0]), .R0(Divisor_r7[0]), .R1(Divisor_r7[1]),
    .R2(Divisor_r7[2]), .R3(Divisor_r7[3]), .R4(Divisor_r7[4]), .R5(Divisor_r7[5]), .R6(Divisor_r7[6]),
    .R7(Divisor_r7[7]));
  Multiplicador8BITs Multiplicador (
    .A0(Resultado_AC[0]), .B0(N[0]), .A1(Resultado_AC[1]), .B1(N[1]), .A2(Resultado_AC[2]), .B2(N[2]),
    .A3(Resultado_AC[3]), .B3(N[3]), .A4(Resultado_AC[4]), .B4(N[4]), .A5(Resultado_AC[5]), .B5(N[5]),
    .A6(Resultado_AC[6]), .B6(N[6]), .A7(Resultado_AC[7]), .B7(N[7]), .AC0(Multiplicador_ac7[0]),
    .AC1(Multiplicador_ac7[1]), .AC2(Multiplicador_ac7[2]), .AC3(Multiplicador_ac7[3]),
    .AC4(Multiplicador_ac7[4]), .AC5(Multiplicador_ac7[5]), .AC6(Multiplicador_ac7[6]),
    .AC7(Multiplicador_ac7[7]), .MQ0(Multiplicador_mq7[0]), .MQ1(Multiplicador_mq7[1]),
    .MQ2(Multiplicador_mq7[2]), .MQ3(Multiplicador_mq7[3]), .MQ4(Multiplicador_mq7[4]),
    .MQ5(Multiplicador_mq7[5]), .MQ6(Multiplicador_mq7[6]), .MQ7(Multiplicador_mq7[7]));
  Somador8BITs Somador (
    .a1(Resultado_AC[0]), .b1(N[0]), .a2(Resultado_AC[1]), .b2(N[1]), .a3(Resultado_AC[2]), .b3(N[2]),
    .a4(Resultado_AC[3]), .b4(N[3]), .cin(1'b0), .a5(Resultado_AC[4]), .b5(N[4]), .a6(Resultado_AC[5]),
    .b6(N[5]), .a7(Resultado_AC[6]), .b7(N[6]), .a8(Resultado_AC[7]), .b8(N[7]), .c1(Somador_c8[0]),
    .c2(Somador_c8[1]), .c3(Somador_c8[2]), .c4(Somador_c8[3]), .c5(Somador_c8[4]), .c6(Somador_c8[5]),
    .c7(Somador_c8[6]), .c8(Somador_c8[7]));  // open: Cout
  Nand8BITs Nand (
    .A0(Resultado_AC[0]), .B0(N[0]), .A1(Resultado_AC[1]), .B1(N[1]), .A2(Resultado_AC[2]), .B2(N[2]),
    .A3(Resultado_AC[3]), .B3(N[3]), .A4(Resultado_AC[4]), .B4(N[4]), .A5(Resultado_AC[5]), .B5(N[5]),
    .A6(Resultado_AC[6]), .B6(N[6]), .A7(Resultado_AC[7]), .B7(N[7]), .Out0(Nand_out0[0]),
    .Out1(Nand_out0[1]), .Out2(Nand_out0[2]), .Out3(Nand_out0[3]), .Out4(Nand_out0[4]), .Out5(Nand_out0[5]),
    .Out6(Nand_out0[6]), .Out7(Nand_out0[7]));
  Xor8BITs Xor (
    .A0(Resultado_AC[0]), .B0(N[0]), .A1(Resultado_AC[1]), .B1(N[1]), .A2(Resultado_AC[2]), .B2(N[2]),
    .A3(Resultado_AC[3]), .B3(N[3]), .A4(Resultado_AC[4]), .B4(N[4]), .A5(Resultado_AC[5]), .B5(N[5]),
    .A6(Resultado_AC[6]), .B6(N[6]), .A7(Resultado_AC[7]), .B7(N[7]), .Out0(Xor_out0[0]), .Out1(Xor_out0[1]),
    .Out2(Xor_out0[2]), .Out3(Xor_out0[3]), .Out4(Xor_out0[4]), .Out5(Xor_out0[5]), .Out6(Xor_out0[6]),
    .Out7(Xor_out0[7]));
  Subtrator8BITs Subtartor (
    .A0(Resultado_AC[0]), .A1(Resultado_AC[1]), .A2(Resultado_AC[2]), .A3(Resultado_AC[3]),
    .A4(Resultado_AC[4]), .A5(Resultado_AC[5]), .A6(Resultado_AC[6]), .A7(Resultado_AC[7]), .B0(N[0]),
    .B1(N[1]), .B2(N[2]), .B3(N[3]), .B4(N[4]), .B5(N[5]), .B6(N[6]), .B7(N[7]), .\_1º (\Subtartor__7º [0]),
    .\_2º (\Subtartor__7º [1]), .\_3º (\Subtartor__7º [2]), .\_4º (\Subtartor__7º [3]),
    .\_5º (\Subtartor__7º [4]), .\_6º (\Subtartor__7º [5]), .\_7º (\Subtartor__7º [6]),
    .\_8º (\Subtartor__7º [7]));
  Multiplexer #(.Selector_Bits(3), .Bits(8)) multiplexer_1 (
    .sel(\Escolher_a_operação ), .in_0(Shift_Right_out7), .in_1(Shift_Left_out7), .in_2(Divisor_q0),
    .in_3(Multiplicador_ac7), .in_4(Somador_c8), .in_5(\Subtartor__7º ), .in_6(Nand_out0), .in_7(Xor_out0),
    .out(multiplexer_1_out));
  Multiplexer #(.Bits(8)) multiplexer_2 (
    .sel(\Divisão_ou_Multiplicação ), .in_0(Divisor_r7), .in_1(Multiplicador_mq7), .out(multiplexer_2_out));
  Registrador8BITs MQ (
    .In0(multiplexer_2_out[0]), .In1(multiplexer_2_out[1]), .In2(multiplexer_2_out[2]),
    .In3(multiplexer_2_out[3]), .In4(multiplexer_2_out[4]), .In5(multiplexer_2_out[5]),
    .In6(multiplexer_2_out[6]), .In7(multiplexer_2_out[7]), .Clock(Clock_MQ), .Out0(Resultado_MQ[0]),
    .Out1(Resultado_MQ[1]), .Out2(Resultado_MQ[2]), .Out3(Resultado_MQ[3]), .Out4(Resultado_MQ[4]),
    .Out5(Resultado_MQ[5]), .Out6(Resultado_MQ[6]), .Out7(Resultado_MQ[7]));
  Registrador8BITs AC (
    .In0(multiplexer_1_out[0]), .In1(multiplexer_1_out[1]), .In2(multiplexer_1_out[2]),
    .In3(multiplexer_1_out[3]), .In4(multiplexer_1_out[4]), .In5(multiplexer_1_out[5]),
    .In6(multiplexer_1_out[6]), .In7(multiplexer_1_out[7]), .Clock(Clock_AC), .Out0(Resultado_AC[0]),
    .Out1(Resultado_AC[1]), .Out2(Resultado_AC[2]), .Out3(Resultado_AC[3]), .Out4(Resultado_AC[4]),
    .Out5(Resultado_AC[5]), .Out6(Resultado_AC[6]), .Out7(Resultado_AC[7]));
endmodule
