// Digital circuit CPU8BITs.dig as structural Verilog
module CPU8BITs (
  input  Reset,
  input  D_ou_M,
  output [7:0] Resultado_AC,
  output [7:0] Resultado_MQ
);

  wire and_1_out, and_2_out, Clock_Principal_out, Maestro_nq, Maestro_q, not_1_out;
  wire [7:0] \Próxima_linha_out , \Próximo_passo_out , register_1_q, \ROM__Memória_d ;

  Button Clock_Principal (.out(Clock_Principal_out));
  T_FF Maestro (.T(1'b1), .C(Clock_Principal_out), .Q(Maestro_q), .nQ(Maestro_nq));
  CounterPreset #(.Bits(8)) \Próximo_passo  (
    .en(1'b1), .C(Clock_Principal_out), .dir(1'b0), .in(\ROM__Memória_d ), .ld(1'b0), .clr(Reset),
    .out(\Próximo_passo_out ));  // open: ovf
  not not_1 (not_1_out, Clock_Principal_out);
  and and_1 (and_1_out, Maestro_nq, not_1_out);
  ROM #(.AddrBits(8), .isProgramMemory("true"), .Bits(8)) \ROM__Memória  (
    .A(\Próximo_passo_out ), .sel(1'b1), .D(\ROM__Memória_d ));
  Register #(.Bits(8)) register_1 (.D(\ROM__Memória_d ), .C(Clock_Principal_out), .en(Maestro_q), .Q(register_1_q));
  and and_2 (and_2_out, Maestro_nq, register_1_q[3]);
  ALU ALU_8_BITs (
    .N(\ROM__Memória_d ), .\Escolher_a_operação (register_1_q[2:0]), .\Divisão_ou_Multiplicação (D_ou_M),
    .Clock_MQ(and_1_out), .Clock_AC(and_1_out), .Resultado(Resultado_AC), .Resultado_2(Resultado_MQ));
  CounterPreset #(.Bits(8)) \Próxima_linha  (
    .en(and_2_out), .C(Clock_Principal_out), .dir(1'b1), .in({8{1'b0}}), .ld(1'b0), .clr(Reset),
    .out(\Próxima_linha_out ));  // open: ovf
  RAMDualPort #(.AddrBits(8), .Bits(8)) \RAM__Memória  (
    .A(\Próxima_linha_out ), .Din(Resultado_AC), .str(and_2_out), .C(Clock_Principal_out), .ld(1'b1));  // open: D

  // Notes on the sheet:
  //   contents of ROM__Memória (hex, n*v repeats v):
  //   c,15,d,5,b,11,a,5
endmodule
