// Digital circuit CélulaDivisora.dig as structural Verilog
module \CélulaDivisora  (
  input  Sor0,
  input  Endo0,
  input  Sor1,
  input  Endo1,
  input  Sor2,
  input  Endo2,
  input  Sor3,
  input  Endo3,
  input  Sor4,
  input  Endo4,
  input  Sor5,
  input  Endo5,
  input  Sor6,
  input  Endo6,
  input  Sor7,
  input  Endo7,
  output R0,
  output R1,
  output R2,
  output R3,
  output R4,
  output R5,
  output R6,
  output R7,
  output Quociente
);

  wire \somadorsubtrator8bits_1__1º , \somadorsubtrator8bits_1__2º , \somadorsubtrator8bits_1__3º ,
       \somadorsubtrator8bits_1__4º , \somadorsubtrator8bits_1__5º , \somadorsubtrator8bits_1__6º ,
       \somadorsubtrator8bits_1__7º , \somadorsubtrator8bits_1__8º ;

  SomadorSubtrator8BITs somadorsubtrator8bits_1 (
    .B0(Endo0), .B1(Endo1), .B2(Endo2), .B3(Endo3), .B4(Endo4), .B5(Endo5), .B6(Endo6), .B7(Endo7),
    .Subtrator(1'b1), .A0(Sor0), .A1(Sor1), .A2(Sor2), .A3(Sor3), .A4(Sor4), .A5(Sor5), .A6(Sor6), .A7(Sor7),
    .\_1º (\somadorsubtrator8bits_1__1º ), .\_2º (\somadorsubtrator8bits_1__2º ),
    .\_3º (\somadorsubtrator8bits_1__3º ), .\_4º (\somadorsubtrator8bits_1__4º ),
    .\_5º (\somadorsubtrator8bits_1__5º ), .\_6º (\somadorsubtrator8bits_1__6º ),
    .\_7º (\somadorsubtrator8bits_1__7º ), .\_8º (\somadorsubtrator8bits_1__8º ), .Cout(Quociente));
  Seletor1Bit seletor1bit_1 (.S1(Quociente), .A0(Endo0), .A1(\somadorsubtrator8bits_1__1º ), .Out(R0));
  Seletor1Bit seletor1bit_2 (.S1(Quociente), .A0(Endo1), .A1(\somadorsubtrator8bits_1__2º ), .Out(R1));
  Seletor1Bit seletor1bit_3 (.S1(Quociente), .A0(Endo2), .A1(\somadorsubtrator8bits_1__3º ), .Out(R2));
  Seletor1Bit seletor1bit_4 (.S1(Quociente), .A0(Endo3), .A1(\somadorsubtrator8bits_1__4º ), .Out(R3));
  Seletor1Bit seletor1bit_5 (.S1(Quociente), .A0(Endo4), .A1(\somadorsubtrator8bits_1__5º ), .Out(R4));
  Seletor1Bit seletor1bit_6 (.S1(Quociente), .A0(Endo5), .A1(\somadorsubtrator8bits_1__6º ), .Out(R5));
  Seletor1Bit seletor1bit_7 (.S1(Quociente), .A0(Endo6), .A1(\somadorsubtrator8bits_1__7º ), .Out(R6));
  Seletor1Bit seletor1bit_8 (.S1(Quociente), .A0(Endo7), .A1(\somadorsubtrator8bits_1__8º ), .Out(R7));
endmodule
