// Digital circuit Divisor8BITs.dig as structural Verilog
module Divisor8BITs (
  input  Sor0,
  input  Sor1,
  input  Sor2,
  input  Sor3,
  input  Sor4,
  input  Sor5,
  input  Sor6,
  input  Sor7,
  input  Endo0,
  input  Endo1,
  input  Endo2,
  input  Endo3,
  input  Endo4,
  input  Endo5,
  input  Endo6,
  input  Endo7,
  output Q7,
  output Q6,
  output Q5,
  output Q4,
  output Q3,
  output Q2,
  output Q1,
  output Q0,
  output R0,
  output R1,
  output R2,
  output R3,
  output R4,
  output R5,
  output R6,
  output R7
);

  wire \céluladivisora_1_r0 , \céluladivisora_1_r1 , \céluladivisora_1_r2 , \céluladivisora_1_r3 ,
       \céluladivisora_1_r4 , \céluladivisora_1_r5 , \céluladivisora_1_r6 , \céluladivisora_2_r0 ,
       \céluladivisora_2_r1 , \céluladivisora_2_r2 , \céluladivisora_2_r3 , \céluladivisora_2_r4 ,
       \céluladivisora_2_r5 , \céluladivisora_2_r6 , \céluladivisora_3_r0 , \céluladivisora_3_r1 ,
       \céluladivisora_3_r2 , \céluladivisora_3_r3 , \céluladivisora_3_r4 , \céluladivisora_3_r5 ,
       \céluladivisora_3_r6 , \céluladivisora_4_r0 , \céluladivisora_4_r1 , \céluladivisora_4_r2 ,
       \céluladivisora_4_r3 , \céluladivisora_4_r4 , \céluladivisora_4_r5 , \céluladivisora_4_r6 ,
       \céluladivisora_5_r0 , \céluladivisora_5_r1 , \céluladivisora_5_r2 , \céluladivisora_5_r3 ,
       \céluladivisora_5_r4 , \céluladivisora_5_r5 , \céluladivisora_5_r6 , \céluladivisora_6_r0 ,
       \céluladivisora_6_r1 , \céluladivisora_6_r2 , \céluladivisora_6_r3 , \céluladivisora_6_r4 ,
       \céluladivisora_6_r5 , \céluladivisora_6_r6 , \céluladivisora_7_r0 , \céluladivisora_7_r1 ,
       \céluladivisora_7_r2 , \céluladivisora_7_r3 , \céluladivisora_7_r4 , \céluladivisora_7_r5 ,
       \céluladivisora_7_r6 ;

  \CélulaDivisora  \céluladivisora_1  (
    .Sor0(Sor0), .Endo0(Endo7), .Sor1(Sor1), .Endo1(1'b0), .Sor2(Sor2), .Endo2(1'b0), .Sor3(Sor3),
    .Endo3(1'b0), .Sor4(Sor4), .Endo4(1'b0), .Sor5(Sor5), .Endo5(1'b0), .Sor6(Sor6), .Endo6(1'b0),
    .Sor7(Sor7), .Endo7(1'b0), .R0(\céluladivisora_1_r0 ), .R1(\céluladivisora_1_r1 ),
    .R2(\céluladivisora_1_r2 ), .R3(\céluladivisora_1_r3 ), .R4(\céluladivisora_1_r4 ),
    .R5(\céluladivisora_1_r5 ), .R6(\céluladivisora_1_r6 ), .Quociente(Q7));  // open: R7
  \CélulaDivisora  \céluladivisora_2  (
    .Sor0(Sor0), .Endo0(Endo6), .Sor1(Sor1), .Endo1(\céluladivisora_1_r0 ), .Sor2(Sor2),
    .Endo2(\céluladivisora_1_r1 ), .Sor3(Sor3), .Endo3(\céluladivisora_1_r2 ), .Sor4(Sor4),
    .Endo4(\céluladivisora_1_r3 ), .Sor5(Sor5), .Endo5(\céluladivisora_1_r4 ), .Sor6(Sor6),
    .Endo6(\céluladivisora_1_r5 ), .Sor7(Sor7), .Endo7(\céluladivisora_1_r6 ), .R0(\céluladivisora_2_r0 ),
    .R1(\céluladivisora_2_r1 ), .R2(\céluladivisora_2_r2 ), .R3(\céluladivisora_2_r3 ),
    .R4(\céluladivisora_2_r4 ), .R5(\céluladivisora_2_r5 ), .R6(\céluladivisora_2_r6 ), .Quociente(Q6));  // open: R7
  \CélulaDivisora  \céluladivisora_3  (
    .Sor0(Sor0), .Endo0(Endo5), .Sor1(Sor1), .Endo1(\céluladivisora_2_r0 ), .Sor2(Sor2),
    .Endo2(\céluladivisora_2_r1 ), .Sor3(Sor3), .Endo3(\céluladivisora_2_r2 ), .Sor4(Sor4),
    .Endo4(\céluladivisora_2_r3 ), .Sor5(Sor5), .Endo5(\céluladivisora_2_r4 ), .Sor6(Sor6),
    .Endo6(\céluladivisora_2_r5 ), .Sor7(Sor7), .Endo7(\céluladivisora_2_r6 ), .R0(\céluladivisora_3_r0 ),
    .R1(\céluladivisora_3_r1 ), .R2(\céluladivisora_3_r2 ), .R3(\céluladivisora_3_r3 ),
    .R4(\céluladivisora_3_r4 ), .R5(\céluladivisora_3_r5 ), .R6(\céluladivisora_3_r6 ), .Quociente(Q5));  // open: R7
  \CélulaDivisora  \céluladivisora_4  (
    .Sor0(Sor0), .Endo0(Endo4), .Sor1(Sor1), .Endo1(\céluladivisora_3_r0 ), .Sor2(Sor2),
    .Endo2(\céluladivisora_3_r1 ), .Sor3(Sor3), .Endo3(\céluladivisora_3_r2 ), .Sor4(Sor4),
    .Endo4(\céluladivisora_3_r3 ), .Sor5(Sor5), .Endo5(\céluladivisora_3_r4 ), .Sor6(Sor6),
    .Endo6(\céluladivisora_3_r5 ), .Sor7(Sor7), .Endo7(\céluladivisora_3_r6 ), .R0(\céluladivisora_4_r0 ),
    .R1(\céluladivisora_4_r1 ), .R2(\céluladivisora_4_r2 ), .R3(\céluladivisora_4_r3 ),
    .R4(\céluladivisora_4_r4 ), .R5(\céluladivisora_4_r5 ), .R6(\céluladivisora_4_r6 ), .Quociente(Q4));  // open: R7
  \CélulaDivisora  \céluladivisora_5  (
    .Sor0(Sor0), .Endo0(Endo3), .Sor1(Sor1), .Endo1(\céluladivisora_4_r0 ), .Sor2(Sor2),
    .Endo2(\céluladivisora_4_r1 ), .Sor3(Sor3), .Endo3(\céluladivisora_4_r2 ), .Sor4(Sor4),
    .Endo4(\céluladivisora_4_r3 ), .Sor5(Sor5), .Endo5(\céluladivisora_4_r4 ), .Sor6(Sor6),
    .Endo6(\céluladivisora_4_r5 ), .Sor7(Sor7), .Endo7(\céluladivisora_4_r6 ), .R0(\céluladivisora_5_r0 ),
    .R1(\céluladivisora_5_r1 ), .R2(\céluladivisora_5_r2 ), .R3(\céluladivisora_5_r3 ),
    .R4(\céluladivisora_5_r4 ), .R5(\céluladivisora_5_r5 ), .R6(\céluladivisora_5_r6 ), .Quociente(Q3));  // open: R7
  \CélulaDivisora  \céluladivisora_6  (
    .Sor0(Sor0), .Endo0(Endo2), .Sor1(Sor1), .Endo1(\céluladivisora_5_r0 ), .Sor2(Sor2),
    .Endo2(\céluladivisora_5_r1 ), .Sor3(Sor3), .Endo3(\céluladivisora_5_r2 ), .Sor4(Sor4),
    .Endo4(\céluladivisora_5_r3 ), .Sor5(Sor5), .Endo5(\céluladivisora_5_r4 ), .Sor6(Sor6),
    .Endo6(\céluladivisora_5_r5 ), .Sor7(Sor7), .Endo7(\céluladivisora_5_r6 ), .R0(\céluladivisora_6_r0 ),
    .R1(\céluladivisora_6_r1 ), .R2(\céluladivisora_6_r2 ), .R3(\céluladivisora_6_r3 ),
    .R4(\céluladivisora_6_r4 ), .R5(\céluladivisora_6_r5 ), .R6(\céluladivisora_6_r6 ), .Quociente(Q2));  // open: R7
  \CélulaDivisora  \céluladivisora_7  (
    .Sor0(Sor0), .Endo0(Endo1), .Sor1(Sor1), .Endo1(\céluladivisora_6_r0 ), .Sor2(Sor2),
    .Endo2(\céluladivisora_6_r1 ), .Sor3(Sor3), .Endo3(\céluladivisora_6_r2 ), .Sor4(Sor4),
    .Endo4(\céluladivisora_6_r3 ), .Sor5(Sor5), .Endo5(\céluladivisora_6_r4 ), .Sor6(Sor6),
    .Endo6(\céluladivisora_6_r5 ), .Sor7(Sor7), .Endo7(\céluladivisora_6_r6 ), .R0(\céluladivisora_7_r0 ),
    .R1(\céluladivisora_7_r1 ), .R2(\céluladivisora_7_r2 ), .R3(\céluladivisora_7_r3 ),
    .R4(\céluladivisora_7_r4 ), .R5(\céluladivisora_7_r5 ), .R6(\céluladivisora_7_r6 ), .Quociente(Q1));  // open: R7
  \CélulaDivisora  \céluladivisora_8  (
    .Sor0(Sor0), .Endo0(Endo0), .Sor1(Sor1), .Endo1(\céluladivisora_7_r0 ), .Sor2(Sor2),
    .Endo2(\céluladivisora_7_r1 ), .Sor3(Sor3), .Endo3(\céluladivisora_7_r2 ), .Sor4(Sor4),
    .Endo4(\céluladivisora_7_r3 ), .Sor5(Sor5), .Endo5(\céluladivisora_7_r4 ), .Sor6(Sor6),
    .Endo6(\céluladivisora_7_r5 ), .Sor7(Sor7), .Endo7(\céluladivisora_7_r6 ), .R0(R0), .R1(R1), .R2(R2),
    .R3(R3), .R4(R4), .R5(R5), .R6(R6), .R7(R7), .Quociente(Q0));

  // Notes on the sheet:
  //   Resultado da Divisão
  //   Resto da Divisão
endmodule
