// Digital circuit Multiplicador2Bits.dig as structural Verilog
module Multiplicador2Bits (
  input  A0,
  input  A1,
  input  B0,
  input  B1,
  output S4,
  output S5,
  output S6,
  output S7
);

  wire and_2_out, and_3_out, and_4_out, somador1bit_1_cout;

  and and_1 (S4, A0, B0);
  and and_2 (and_2_out, A1, B0);
  and and_3 (and_3_out, A0, B1);
  and and_4 (and_4_out, B1, A1);
  Somador1BIT somador1bit_1 (.A0(and_2_out), .A1(and_3_out), .Cin(1'b0), .Sum(S5), .Cout(somador1bit_1_cout));
  Somador1BIT somador1bit_2 (.A0(and_4_out), .A1(somador1bit_1_cout), .Cin(1'b0), .Sum(S6), .Cout(S7));
endmodule
