// Digital circuit Multiplicador4BITs.dig as structural Verilog
module Multiplicador4BITs (
  input  A3,
  input  A2,
  input  A1,
  input  A0,
  input  B3,
  input  B2,
  input  B1,
  input  B0,
  output S0,
  output S1,
  output S2,
  output S3,
  output S4,
  output S5,
  output S6,
  output S7
);

  wire multiplicador2bits_1_s4, multiplicador2bits_1_s5, multiplicador2bits_1_s6, multiplicador2bits_1_s7,
       multiplicador2bits_2_s4, multiplicador2bits_2_s5, multiplicador2bits_2_s6, multiplicador2bits_2_s7,
       multiplicador2bits_3_s4, multiplicador2bits_3_s5, multiplicador2bits_3_s6, multiplicador2bits_3_s7,
       multiplicador2bits_4_s4, multiplicador2bits_4_s5, multiplicador2bits_4_s6, multiplicador2bits_4_s7,
       somador4bits_1_c1, somador4bits_1_c2, somador4bits_1_c3, somador4bits_1_c4, somador4bits_1_cout;

  Multiplicador2Bits multiplicador2bits_1 (
    .A0(A0), .A1(A1), .B0(B0), .B1(B1), .S4(multiplicador2bits_1_s4), .S5(multiplicador2bits_1_s5),
    .S6(multiplicador2bits_1_s6), .S7(multiplicador2bits_1_s7));
  Multiplicador2Bits multiplicador2bits_2 (
    .A0(A2), .A1(A3), .B0(B0), .B1(B1), .S4(multiplicador2bits_2_s4), .S5(multiplicador2bits_2_s5),
    .S6(multiplicador2bits_2_s6), .S7(multiplicador2bits_2_s7));
  Multiplicador2Bits multiplicador2bits_3 (
    .A0(A0), .A1(A1), .B0(B2), .B1(B3), .S4(multiplicador2bits_3_s4), .S5(multiplicador2bits_3_s5),
    .S6(multiplicador2bits_3_s6), .S7(multiplicador2bits_3_s7));
  Multiplicador2Bits multiplicador2bits_4 (
    .A0(A2), .A1(A3), .B0(B2), .B1(B3), .S4(multiplicador2bits_4_s4), .S5(multiplicador2bits_4_s5),
    .S6(multiplicador2bits_4_s6), .S7(multiplicador2bits_4_s7));
  Somador4BITs somador4bits_1 (
    .A1(multiplicador2bits_2_s4), .B1(multiplicador2bits_3_s4), .A2(multiplicador2bits_2_s5),
    .B2(multiplicador2bits_3_s5), .A3(multiplicador2bits_2_s6), .B3(multiplicador2bits_3_s6),
    .A4(multiplicador2bits_2_s7), .B4(multiplicador2bits_3_s7), .Cin(1'b0), .c1(somador4bits_1_c1),
    .c2(somador4bits_1_c2), .c3(somador4bits_1_c3), .c4(somador4bits_1_c4), .Cout(somador4bits_1_cout));
  Somador8BITs somador8bits_1 (
    .a1(multiplicador2bits_1_s4), .b1(1'b0), .a2(multiplicador2bits_1_s5), .b2(1'b0),
    .a3(multiplicador2bits_1_s6), .b3(somador4bits_1_c1), .a4(multiplicador2bits_1_s7),
    .b4(somador4bits_1_c2), .cin(1'b0), .a5(multiplicador2bits_4_s4), .b5(somador4bits_1_c3),
    .a6(multiplicador2bits_4_s5), .b6(somador4bits_1_c4), .a7(multiplicador2bits_4_s6),
    .b7(somador4bits_1_cout), .a8(multiplicador2bits_4_s7), .b8(1'b0), .c1(S0), .c2(S1), .c3(S2), .c4(S3),
    .c5(S4), .c6(S5), .c7(S6), .c8(S7));  // open: Cout

  // Notes on the sheet:
  //   De cima
  //   Vezes
  //   De baixo
endmodule
