// Digital circuit Multiplicador8BITs.dig as structural Verilog
module Multiplicador8BITs (
  input  A0,
  input  B0,
  input  A1,
  input  B1,
  input  A2,
  input  B2,
  input  A3,
  input  B3,
  input  A4,
  input  B4,
  input  A5,
  input  B5,
  input  A6,
  input  B6,
  input  A7,
  input  B7,
  output AC0,
  output AC1,
  output AC2,
  output AC3,
  output AC4,
  output AC5,
  output AC6,
  output AC7,
  output MQ0,
  output MQ1,
  output MQ2,
  output MQ3,
  output MQ4,
  output MQ5,
  output MQ6,
  output MQ7
);

  wire multiplicador4bits_1_s0, multiplicador4bits_1_s1, multiplicador4bits_1_s2, multiplicador4bits_1_s3,
       multiplicador4bits_1_s4, multiplicador4bits_1_s5, multiplicador4bits_1_s6, multiplicador4bits_1_s7,
       multiplicador4bits_2_s0, multiplicador4bits_2_s1, multiplicador4bits_2_s2, multiplicador4bits_2_s3,
       multiplicador4bits_2_s4, multiplicador4bits_2_s5, multiplicador4bits_2_s6, multiplicador4bits_2_s7,
       multiplicador4bits_3_s0, multiplicador4bits_3_s1, multiplicador4bits_3_s2, multiplicador4bits_3_s3,
       multiplicador4bits_3_s4, multiplicador4bits_3_s5, multiplicador4bits_3_s6, multiplicador4bits_3_s7,
       multiplicador4bits_4_s0, multiplicador4bits_4_s1, multiplicador4bits_4_s2, multiplicador4bits_4_s3,
       multiplicador4bits_4_s4, multiplicador4bits_4_s5, multiplicador4bits_4_s6, multiplicador4bits_4_s7,
       somador8bits_1_c1, somador8bits_1_c2, somador8bits_1_c3, somador8bits_1_c4, somador8bits_1_c5,
       somador8bits_1_c6, somador8bits_1_c7, somador8bits_1_c8, somador8bits_1_cout, somador8bits_2_cout;

  Multiplicador4BITs multiplicador4bits_1 (
    .A3(A3), .A2(A2), .A1(A1), .A0(A0), .B3(B3), .B2(B2), .B1(B1), .B0(B0), .S0(multiplicador4bits_1_s0),
    .S1(multiplicador4bits_1_s1), .S2(multiplicador4bits_1_s2), .S3(multiplicador4bits_1_s3),
    .S4(multiplicador4bits_1_s4), .S5(multiplicador4bits_1_s5), .S6(multiplicador4bits_1_s6),
    .S7(multiplicador4bits_1_s7));
  Multiplicador4BITs multiplicador4bits_2 (
    .A3(A7), .A2(A6), .A1(A5), .A0(A4), .B3(B3), .B2(B2), .B1(B1), .B0(B0), .S0(multiplicador4bits_2_s0),
    .S1(multiplicador4bits_2_s1), .S2(multiplicador4bits_2_s2), .S3(multiplicador4bits_2_s3),
    .S4(multiplicador4bits_2_s4), .S5(multiplicador4bits_2_s5), .S6(multiplicador4bits_2_s6),
    .S7(multiplicador4bits_2_s7));
  Multiplicador4BITs multiplicador4bits_3 (
    .A3(A3), .A2(A2), .A1(A1), .A0(A0), .B3(B7), .B2(B6), .B1(B5), .B0(B4), .S0(multiplicador4bits_3_s0),
    .S1(multiplicador4bits_3_s1), .S2(multiplicador4bits_3_s2), .S3(multiplicador4bits_3_s3),
    .S4(multiplicador4bits_3_s4), .S5(multiplicador4bits_3_s5), .S6(multiplicador4bits_3_s6),
    .S7(multiplicador4bits_3_s7));
  Multiplicador4BITs multiplicador4bits_4 (
    .A3(A7), .A2(A6), .A1(A5), .A0(A4), .B3(B7), .B2(B6), .B1(B5), .B0(B4), .S0(multiplicador4bits_4_s0),
    .S1(multiplicador4bits_4_s1), .S2(multiplicador4bits_4_s2), .S3(multiplicador4bits_4_s3),
    .S4(multiplicador4bits_4_s4), .S5(multiplicador4bits_4_s5), .S6(multiplicador4bits_4_s6),
    .S7(multiplicador4bits_4_s7));
  Somador8BITs somador8bits_1 (
    .a1(multiplicador4bits_2_s0), .b1(multiplicador4bits_3_s0), .a2(multiplicador4bits_2_s1),
    .b2(multiplicador4bits_3_s1), .a3(multiplicador4bits_2_s2), .b3(multiplicador4bits_3_s2),
    .a4(multiplicador4bits_2_s3), .b4(multiplicador4bits_3_s3), .cin(1'b0), .a5(multiplicador4bits_2_s4),
    .b5(multiplicador4bits_3_s4), .a6(multiplicador4bits_2_s5), .b6(multiplicador4bits_3_s5),
    .a7(multiplicador4bits_2_s6), .b7(multiplicador4bits_3_s6), .a8(multiplicador4bits_2_s7),
    .b8(multiplicador4bits_3_s7), .c1(somador8bits_1_c1), .c2(somador8bits_1_c2), .c3(somador8bits_1_c3),
    .c4(somador8bits_1_c4), .c5(somador8bits_1_c5), .c6(somador8bits_1_c6), .c7(somador8bits_1_c7),
    .c8(somador8bits_1_c8), .Cout(somador8bits_1_cout));
  Somador8BITs somador8bits_2 (
    .a1(multiplicador4bits_1_s0), .b1(1'b0), .a2(multiplicador4bits_1_s1), .b2(1'b0),
    .a3(multiplicador4bits_1_s2), .b3(1'b0), .a4(multiplicador4bits_1_s3), .b4(1'b0), .cin(1'b0),
    .a5(multiplicador4bits_1_s4), .b5(somador8bits_1_c1), .a6(multiplicador4bits_1_s5),
    .b6(somador8bits_1_c2), .a7(multiplicador4bits_1_s6), .b7(somador8bits_1_c3),
    .a8(multiplicador4bits_1_s7), .b8(somador8bits_1_c4), .c1(AC0), .c2(AC1), .c3(AC2), .c4(AC3), .c5(AC4),
    .c6(AC5), .c7(AC6), .c8(AC7), .Cout(somador8bits_2_cout));
  Somador8BITs somador8bits_3 (
    .a1(multiplicador4bits_4_s0), .b1(somador8bits_1_c5), .a2(multiplicador4bits_4_s1),
    .b2(somador8bits_1_c6), .a3(multiplicador4bits_4_s2), .b3(somador8bits_1_c7),
    .a4(multiplicador4bits_4_s3), .b4(somador8bits_1_c8), .cin(somador8bits_2_cout),
    .a5(multiplicador4bits_4_s4), .b5(somador8bits_1_cout), .a6(multiplicador4bits_4_s5), .b6(1'b0),
    .a7(multiplicador4bits_4_s6), .b7(1'b0), .a8(multiplicador4bits_4_s7), .b8(1'b0), .c1(MQ0), .c2(MQ1),
    .c3(MQ2), .c4(MQ3), .c5(MQ4), .c6(MQ5), .c7(MQ6), .c8(MQ7));  // open: Cout
endmodule
