// Digital circuit Nand8BITs.dig as structural Verilog
module Nand8BITs (
  input  A0,
  input  B0,
  input  A1,
  input  B1,
  input  A2,
  input  B2,
  input  A3,
  input  B3,
  input  A4,
  input  B4,
  input  A5,
  input  B5,
  input  A6,
  input  B6,
  input  A7,
  input  B7,
  output Out0,
  output Out1,
  output Out2,
  output Out3,
  output Out4,
  output Out5,
  output Out6,
  output Out7
);

  nand nand_1 (Out0, A0, B0);
  nand nand_2 (Out1, A1, B1);
  nand nand_3 (Out2, A2, B2);
  nand nand_4 (Out3, A3, B3);
  nand nand_5 (Out4, A4, B4);
  nand nand_6 (Out5, A5, B5);
  nand nand_7 (Out6, A6, B6);
  nand nand_8 (Out7, A7, B7);
endmodule
