// Digital circuit Registrador8BITs.dig as structural Verilog
module Registrador8BITs (
  input  In0,
  input  In1,
  input  In2,
  input  In3,
  input  In4,
  input  In5,
  input  In6,
  input  In7,
  input  Clock,
  output Out0,
  output Out1,
  output Out2,
  output Out3,
  output Out4,
  output Out5,
  output Out6,
  output Out7
);

  D_FF d_ff_1 (.D(In0), .C(Clock), .Q(Out0));  // open: nQ
  D_FF d_ff_2 (.D(In1), .C(Clock), .Q(Out1));  // open: nQ
  D_FF d_ff_3 (.D(In2), .C(Clock), .Q(Out2));  // open: nQ
  D_FF d_ff_4 (.D(In3), .C(Clock), .Q(Out3));  // open: nQ
  D_FF d_ff_5 (.D(In4), .C(Clock), .Q(Out4));  // open: nQ
  D_FF d_ff_6 (.D(In5), .C(Clock), .Q(Out5));  // open: nQ
  D_FF d_ff_7 (.D(In6), .C(Clock), .Q(Out6));  // open: nQ
  D_FF d_ff_8 (.D(In7), .C(Clock), .Q(Out7));  // open: nQ
endmodule
