// Digital circuit Seletor1Bit.dig as structural Verilog
module Seletor1Bit (
  input  S1,
  input  A0,
  input  A1,
  output Out
);

  wire and_1_out, and_2_out, not_1_out;

  not not_1 (not_1_out, S1);
  and and_1 (and_1_out, A0, not_1_out);
  and and_2 (and_2_out, A1, S1);
  or or_1 (Out, and_1_out, and_2_out);
endmodule
