// Digital circuit Somador1BIT.dig as structural Verilog
module Somador1BIT (
  input  A0,
  input  A1,
  input  Cin,
  output Sum,
  output Cout
);

  wire and_1_out, and_2_out, and_3_out, xor_1_out;

  xor xor_1 (xor_1_out, A0, A1);
  and and_1 (and_1_out, A0, A1);
  and and_2 (and_2_out, Cin, A0);
  and and_3 (and_3_out, A1, Cin);
  or or_1 (Cout, and_1_out, and_2_out, and_3_out);
  xor xor_2 (Sum, xor_1_out, Cin);
endmodule
