// Digital circuit Somador4BITs.dig as structural Verilog
module Somador4BITs (
  input  A1,
  input  B1,
  input  A2,
  input  B2,
  input  A3,
  input  B3,
  input  A4,
  input  B4,
  input  Cin,
  output c1,
  output c2,
  output c3,
  output c4,
  output Cout
);

  wire somador1bit_2_cout, somador1bit_3_cout, somador1bit_4_cout;

  Somador1BIT somador1bit_1 (.A0(A4), .A1(B4), .Cin(somador1bit_2_cout), .Sum(c4), .Cout(Cout));
  Somador1BIT somador1bit_2 (.A0(A3), .A1(B3), .Cin(somador1bit_3_cout), .Sum(c3), .Cout(somador1bit_2_cout));
  Somador1BIT somador1bit_3 (.A0(A2), .A1(B2), .Cin(somador1bit_4_cout), .Sum(c2), .Cout(somador1bit_3_cout));
  Somador1BIT somador1bit_4 (.A0(A1), .A1(B1), .Cin(Cin), .Sum(c1), .Cout(somador1bit_4_cout));
endmodule
