// Digital circuit Somador8BITs.dig as structural Verilog
module Somador8BITs (
  input  a1,
  input  b1,
  input  a2,
  input  b2,
  input  a3,
  input  b3,
  input  a4,
  input  b4,
  input  cin,
  input  a5,
  input  b5,
  input  a6,
  input  b6,
  input  a7,
  input  b7,
  input  a8,
  input  b8,
  output c1,
  output c2,
  output c3,
  output c4,
  output c5,
  output c6,
  output c7,
  output c8,
  output Cout
);

  wire somador4bits_1_cout;

  Somador4BITs somador4bits_1 (
    .A1(a1), .B1(b1), .A2(a2), .B2(b2), .A3(a3), .B3(b3), .A4(a4), .B4(b4), .Cin(cin), .c1(c1), .c2(c2),
    .c3(c3), .c4(c4), .Cout(somador4bits_1_cout));
  Somador4BITs somador4bits_2 (
    .A1(a5), .B1(b5), .A2(a6), .B2(b6), .A3(a7), .B3(b7), .A4(a8), .B4(b8), .Cin(somador4bits_1_cout),
    .c1(c5), .c2(c6), .c3(c7), .c4(c8), .Cout(Cout));
endmodule
