// Digital circuit SomadorGeral8BITS.dig as structural Verilog
module SomadorGeral8BITS (
  input  _1,
  input  _1_2,
  input  _2,
  input  _2_2,
  input  _4,
  input  _4_2,
  input  _8,
  input  _8_2,
  input  _16,
  input  _16_2,
  input  _32,
  input  _32_2,
  input  _64,
  input  _64_2,
  input  _128,
  input  _128_2,
  output \_1º ,
  output \_2º ,
  output \_3º ,
  output \_4º ,
  output \_5º ,
  output \_6º ,
  output \_7º ,
  output \_8º ,
  output OverFlow
);

  Somador8BITs somador8bits_1 (
    .a1(_1), .b1(_1_2), .a2(_2), .b2(_2_2), .a3(_4), .b3(_4_2), .a4(_8), .b4(_8_2), .cin(1'b0), .a5(_16),
    .b5(_16_2), .a6(_32), .b6(_32_2), .a7(_64), .b7(_64_2), .a8(_128), .b8(_128_2), .c1(\_1º ), .c2(\_2º ),
    .c3(\_3º ), .c4(\_4º ), .c5(\_5º ), .c6(\_6º ), .c7(\_7º ), .c8(\_8º ), .Cout(OverFlow));
endmodule
