// Digital circuit SomadorSubtrator8BITs.dig as structural Verilog
module SomadorSubtrator8BITs (
  input  B0,
  input  B1,
  input  B2,
  input  B3,
  input  B4,
  input  B5,
  input  B6,
  input  B7,
  input  Subtrator,
  input  A0,
  input  A1,
  input  A2,
  input  A3,
  input  A4,
  input  A5,
  input  A6,
  input  A7,
  output \_1º ,
  output \_2º ,
  output \_3º ,
  output \_4º ,
  output \_5º ,
  output \_6º ,
  output \_7º ,
  output \_8º ,
  output Cout
);

  wire xor_1_out, xor_2_out, xor_3_out, xor_4_out, xor_5_out, xor_6_out, xor_7_out, xor_8_out;

  xor xor_1 (xor_1_out, A0, Subtrator);
  xor xor_2 (xor_2_out, A1, Subtrator);
  xor xor_3 (xor_3_out, A2, Subtrator);
  xor xor_4 (xor_4_out, A3, Subtrator);
  xor xor_5 (xor_5_out, A4, Subtrator);
  xor xor_6 (xor_6_out, A5, Subtrator);
  xor xor_7 (xor_7_out, A6, Subtrator);
  xor xor_8 (xor_8_out, A7, Subtrator);
  Somador8BITs somador8bits_1 (
    .a1(B0), .b1(xor_1_out), .a2(B1), .b2(xor_2_out), .a3(B2), .b3(xor_3_out), .a4(B3), .b4(xor_4_out),
    .cin(Subtrator), .a5(B4), .b5(xor_5_out), .a6(B5), .b6(xor_6_out), .a7(B6), .b7(xor_7_out), .a8(B7),
    .b8(xor_8_out), .c1(\_1º ), .c2(\_2º ), .c3(\_3º ), .c4(\_4º ), .c5(\_5º ), .c6(\_6º ), .c7(\_7º ),
    .c8(\_8º ), .Cout(Cout));
endmodule
