// Digital circuit Subtrator8BITs.dig as structural Verilog
module Subtrator8BITs (
  input  A0,
  input  A1,
  input  A2,
  input  A3,
  input  A4,
  input  A5,
  input  A6,
  input  A7,
  input  B0,
  input  B1,
  input  B2,
  input  B3,
  input  B4,
  input  B5,
  input  B6,
  input  B7,
  output \_1º ,
  output \_2º ,
  output \_3º ,
  output \_4º ,
  output \_5º ,
  output \_6º ,
  output \_7º ,
  output \_8º 
);

  wire not_1_out, not_2_out, not_3_out, not_4_out, not_5_out, not_6_out, not_7_out, not_8_out;

  not not_1 (not_1_out, B0);
  not not_2 (not_2_out, B1);
  not not_3 (not_3_out, B2);
  not not_4 (not_4_out, B3);
  not not_5 (not_5_out, B4);
  not not_6 (not_6_out, B5);
  not not_7 (not_7_out, B6);
  not not_8 (not_8_out, B7);
  Somador8BITs somador8bits_1 (
    .a1(A0), .b1(not_1_out), .a2(A1), .b2(not_2_out), .a3(A2), .b3(not_3_out), .a4(A3), .b4(not_4_out),
    .cin(1'b1), .a5(A4), .b5(not_5_out), .a6(A5), .b6(not_6_out), .a7(A6), .b7(not_7_out), .a8(A7),
    .b8(not_8_out), .c1(\_1º ), .c2(\_2º ), .c3(\_3º ), .c4(\_4º ), .c5(\_5º ), .c6(\_6º ), .c7(\_7º ),
    .c8(\_8º ));  // open: Cout
endmodule
